# Fritzing sketch 2023_power_circuit (saved by Fritzing 0.9.10b)

parts:
  PDH1 = rev_pdh
  BAT1 = Battery 12V [package=battcom_20mm_pth]  # not connected
  BLDC1 = CTRE Falcon 500 [part_number=19-708850]
  BLDC2 = CTRE Falcon 500 [part_number=19-708850]
  Mini_Power_Module1 = REV Mini Power Module [form="♀ (female)" package=THT]
  ctrl1 = rev_spark_max [part_number=rev-11-2158]
  ctrl2 = rev_spark_max [part_number=rev-11-2158]
  CANcoder1 = CTRE CANcoder [package=THT]
  BLDC4 = CTRE Falcon 500 [part_number=19-708850]
  BLDC5 = CTRE Falcon 500 [part_number=19-708850]
  BLDC6 = CTRE Falcon 500 [part_number=19-708850]
  VR1 = LM2577 (TO263) [part_number=LM2577 package=TO263]  # not connected
  CB1 = Thermal Circuit Breaker [package=waterproof]  # not connected
  Pigeon_2_1 = CTRE Pigeon 2.0 [package=THT]
  775-Pro_Brushed_Motor1 = 775-Pro Brushed Motor [form="♀ (female)" package=THT]
  775-Pro_Brushed_Motor2 = 775-Pro Brushed Motor [form="♀ (female)" package=THT]
  CANivore1 = CTRE CANivore [form="♀ (female)" package=THT]
  CANcoder4 = CTRE CANcoder [package=THT]
  CANcoder5 = CTRE CANcoder [package=THT]
  Mod2 = VRM
  CANcoder6 = CTRE CANcoder [package=THT]  # not connected
  BLDC7 = CTRE Falcon 500 [part_number=19-708850]  # not connected
  BLDC8 = CTRE Falcon 500 [part_number=19-708850]  # not connected
  BLDC9 = CTRE Falcon 500 [part_number=19-708850]  # not connected
  BLDC10 = CTRE Falcon 500 [part_number=19-708850]  # not connected
  BLDC11 = CTRE Falcon 500 [part_number=19-708850]  # not connected
  BLDC12 = CTRE Falcon 500 [part_number=19-708850]  # not connected
  BLDC13 = CTRE Falcon 500 [part_number=19-708850]  # not connected
  TBE1 = REV Through Bore Encoder  # not connected
  J1 = Generic female header - 7 pins [form="♀ (female)" package=THT]  # not connected
  J2 = Generic female header - 3 pins [form="♀ (female)" package=THT]  # not connected
  J3 = Generic female header - 3 pins [form="♀ (female)" package=THT]  # not connected

nets:
  N1: PDH1.connector0, BLDC1.Vin+
  N2: PDH1.connector1, BLDC1.Vin-
  N3: PDH1.connector2, BLDC2.Vin+
  N4: PDH1.connector3, BLDC2.Vin-
  N5: PDH1.connector4, Mini_Power_Module1.Input_+
  N6: PDH1.connector5, Mini_Power_Module1.Input_-
  N7: PDH1.connector6, BLDC4.Vin+
  N8: PDH1.connector7, BLDC4.Vin-
  N9: PDH1.connector8, BLDC5.Vin+
  N10: PDH1.connector9, BLDC5.Vin-
  N11: PDH1.connector10, ctrl2.connector0
  N12: PDH1.connector11, ctrl2.connector1
  N13: PDH1.connector12, ctrl1.connector0
  N14: PDH1.connector13, ctrl1.connector1
  N15: PDH1.connector14, BLDC6.Vin+
  N16: PDH1.connector15, BLDC6.Vin-
  N17: Mini_Power_Module1.5+, CANcoder4.+
  N18: Mini_Power_Module1.5-, CANcoder4.-
  N19: Mini_Power_Module1.4+, Pigeon_2_1.+
  N20: Mini_Power_Module1.4-, Pigeon_2_1.-
  N21: Mini_Power_Module1.3+, CANcoder5.+
  N22: Mini_Power_Module1.3-, CANcoder5.-
  N23: Mini_Power_Module1.2+, Mod2.In12V
  N24: Mini_Power_Module1.2-, Mod2.5V_2A_GND0, Mod2.InGnd
  N25: Mini_Power_Module1.1+, CANivore1.V+[R]
  N26: Mini_Power_Module1.1-, CANivore1.V-[B]
  N27: Mini_Power_Module1.0+, CANcoder1.+
  N28: Mini_Power_Module1.0-, CANcoder1.-
  N29: ctrl1.connector2, 775-Pro_Brushed_Motor1.pin1
  N30: ctrl1.connector3, 775-Pro_Brushed_Motor1.pin2
  N31: ctrl2.connector2, 775-Pro_Brushed_Motor2.pin1
  N32: ctrl2.connector3, 775-Pro_Brushed_Motor2.pin2

custom parts:
  Battery 12V: Battery Holders Various common sizes : AA, AAA, 20mm coin cell and 12mm coin cell.
  CTRE Falcon 500: The Falcon 500 powered by Talon FX is a brushless motor with an integrated motor controller and high-resolution encoder, custom designed specifically for the FIRST Robotics Competition, through a collaboration between Cross the Road Electronics and VEX Robotics.
  REV Mini Power Module: Generic female header
  Thermal Circuit Breaker: Cooper Bussman P/N CB185-120, CB185F-120, CB285-120 CB285F-120, CB285120F or Optifuse P/N 153120, 253120
  CTRE Pigeon 2.0: Generic single row SMD female header
  REV Through Bore Encoder: The REV Through Bore Encoder is specifically designed with the end user in mind, allowing teams to place sensors in the locations closest to the rotation that they wish to measure. This rotary sensor measures both relative and absolute position through its ABI quadrature output and its absolute position pulse output. Mounting an encoder has never been easier with a 1/2in Hex Through Bore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
  Generic female header - 7 pins: Generic female header
  Generic female header - 3 pins: Generic female header
